# Fritzing sketch alpha (saved by Fritzing 0.7.10b)
breadboards: 1

parts:
  Part1 = XBee Explorer Regulated
  T1 = LM35 Temperature Sensor [package="TO92 [THT]"]
  Arduino1 = Arduino

nets:
  GND: Part1.GND, T1.GND, Arduino1.GND
  N1: Part1.DIO2, T1.Vout
  5V: Part1.5V, T1.+Vs, Arduino1.+5V
